// Logisim project Proj 1.circ as structural Verilog: 23 circuits, main circuit MIPS32
module MIPS32 (
);

  wire and_1_out, clock_1_out, decode_1_branch_not_jump, decode_1_jump_branch_enable, decode_1_link,
       decode_1_load_store_byte_vs_word, decode_1_mux1, decode_1_mux2, decode_1_r_type_jump, decode_1_sasel,
       decode_1_signed, decode_1_writeenable1, decode_1_writeenable2, disable_jump_1_jump_out,
       disable_jump_1_mux2_out, disable_jump_1_wed_out, disable_jump_1_wer_out, disable_load_1_jump_out,
       disable_load_1_mux2_out, disable_load_1_wed_out, disable_load_1_wer_out, execute_1_jump_out,
       execute_1_load_fwd, execute_1_wer_out, isolate34_1_byte_out, isolate34_1_jump_branch_out,
       isolate34_1_link_out, isolate34_1_signed_out, isolate34_1_wbmux_out, isolate34_1_wed_out,
       isolate34_1_wer_out, isolator_2_3_1_branchnotjump_out, isolator_2_3_1_byte_out,
       isolator_2_3_1_immmux_out, isolator_2_3_1_jr_out, isolator_2_3_1_jump_out, isolator_2_3_1_link_out,
       isolator_2_3_1_sasel_out, isolator_2_3_1_signed_out, isolator_2_3_1_wbmux_out, isolator_2_3_1_wed_out,
       isolator_2_3_1_wer_out, not_1_out, registerfile_1_p3;
  wire [1:0] decode_1_extend;
  wire [2:0] decode_1_comp_code, isolator_2_3_1_compcode_out;
  wire [3:0] decode_1_alu_code, isolator_2_3_1_alu_out, memoryhelp_1_sel;
  wire [4:0] isolate34_1_rd_out, isolator_2_3_1_rd_out, isolator_2_3_1_rs_out, isolator_2_3_1_rt_out,
       isolator_2_3_1_sa_out, linking_1_rd_out, multiplexer_1_out, registerfile_1_p4, split_1_rd, split_1_rs,
       split_1_rt, split_1_shamt;
  wire [5:0] split_1_func, split_1_op;
  wire [15:0] split_1_imm;
  wire [19:0] memoryhelp_1_a;
  wire [25:0] split_1_instrindex;
  wire [31:0] bitextend_1_imm_out, branchmux_1_newpc, byteextract_1_output, count_1_1_pc_4, execute_1_b_out,
       execute_1_c_out, isolate12_1_instr_out, isolate12_1_pc_out, isolate34_1_c_out,
       isolate34_1_linkaddress_out, isolate34_1_write_out, isolator_2_3_1_a_out, isolator_2_3_1_b_out,
       isolator_2_3_1_imm_out, isolator_2_3_1_pc_out, linking_1_c_out, memoryhelp_1_write_out, mips_ram_1_p7,
       mipsprogramrom_1_p2, multiplexer_2_out, register_1_q, registerfile_1_p1, registerfile_1_p7,
       registerfile_1_p8;

  Clock clock_1 (.out(clock_1_out));
  Count__1 count_1_1 (.PC(branchmux_1_newpc), .PC_4(count_1_1_pc_4));
  not not_1 (not_1_out, and_1_out);
  BranchMux branchmux_1 (
    .PC_4(register_1_q), .JumpAddress(isolate34_1_c_out), .NewPC(branchmux_1_newpc),
    .Jump_Branch(isolate34_1_jump_branch_out));
  Register #(.width(32)) register_1 (
    .D(count_1_1_pc_4), .en(not_1_out), .Q(register_1_q), .clk(clock_1_out));  // open: clr
  // MIPSProgramROM mipsprogramrom_1: pin names not known; wires that end beside it: branchmux_1_newpc, mipsprogramrom_1_p2
  Isolate12 isolate12_1 (
    .PC_in(branchmux_1_newpc), .Instr_in(mipsprogramrom_1_p2), .clock(clock_1_out),
    .PC_out(isolate12_1_pc_out), .Instr_out(isolate12_1_instr_out), .Disable(and_1_out));
  Split split_1 (
    .Instr(isolate12_1_instr_out), .Func(split_1_func), .shamt(split_1_shamt), .rd(split_1_rd),
    .Imm(split_1_imm), .rt(split_1_rt), .rs(split_1_rs), .InstrIndex(split_1_instrindex), .Op(split_1_op));
  BitExtend bitextend_1 (
    .BitEx(decode_1_extend), .Jump(decode_1_jump_branch_enable), .Imm_In(split_1_imm),
    .InstrIndex(split_1_instrindex), .Imm_Out(bitextend_1_imm_out));
  Decode decode_1 (
    .SAsel(decode_1_sasel), .ALU_code(decode_1_alu_code), .MUX1(decode_1_mux1), .Op(split_1_op),
    .MUX2(decode_1_mux2), .WriteEnable1(decode_1_writeenable1), .WriteEnable2(decode_1_writeenable2),
    .Signed(decode_1_signed), .Func(split_1_func), .Extend(decode_1_extend),
    .Load_Store_Byte_vs_Word(decode_1_load_store_byte_vs_word),
    .Jump_Branch_Enable(decode_1_jump_branch_enable), .Link(decode_1_link), .rt(split_1_rt),
    .Comp_Code(decode_1_comp_code), .Branch_not_Jump(decode_1_branch_not_jump),
    .R_type_Jump(decode_1_r_type_jump));
  Disable_Jump disable_jump_1 (
    .WER_in(decode_1_writeenable1), .Jump(isolate34_1_jump_branch_out), .WED_in(decode_1_writeenable2),
    .WER_out(disable_jump_1_wer_out), .WED_out(disable_jump_1_wed_out),
    .Jump_in(decode_1_jump_branch_enable), .Jump_out(disable_jump_1_jump_out),
    .Mux2_out(disable_jump_1_mux2_out), .Mux2_in(decode_1_mux2));
  // RegisterFile registerfile_1: pin names not known; wires that end beside it: registerfile_1_p1, clock_1_out, registerfile_1_p3, registerfile_1_p4, split_1_rs, split_1_rt, registerfile_1_p7, registerfile_1_p8
  Multiplexer #(.width(5), .enable("false")) multiplexer_1 (
    .in0(split_1_rd), .in1(split_1_rt), .out(multiplexer_1_out), .sel(decode_1_mux1));
  Isolator_2_3 isolator_2_3_1 (
    .rs_in(split_1_rs), .rt_in(split_1_rt), .PC_in(isolate12_1_pc_out), .Imm_in(bitextend_1_imm_out),
    .A_in(registerfile_1_p7), .B_in(registerfile_1_p8), .rd_in(multiplexer_1_out), .sa_in(split_1_shamt),
    .ALU_in(decode_1_alu_code), .ImmMux_in(decode_1_mux1), .WBMUX_in(disable_jump_1_mux2_out),
    .WER_in(disable_jump_1_wer_out), .WED_in(disable_jump_1_wed_out), .Signed_in(decode_1_signed),
    .clock(clock_1_out), .rs_out(isolator_2_3_1_rs_out), .rt_out(isolator_2_3_1_rt_out),
    .PC_out(isolator_2_3_1_pc_out), .Imm_out(isolator_2_3_1_imm_out), .A_out(isolator_2_3_1_a_out),
    .B_out(isolator_2_3_1_b_out), .rd_out(isolator_2_3_1_rd_out), .sa_out(isolator_2_3_1_sa_out),
    .ALU_out(isolator_2_3_1_alu_out), .ImmMux_out(isolator_2_3_1_immmux_out),
    .WBMUX_out(isolator_2_3_1_wbmux_out), .WER_out(isolator_2_3_1_wer_out), .WED_out(isolator_2_3_1_wed_out),
    .Signed_out(isolator_2_3_1_signed_out), .Byte_in(decode_1_load_store_byte_vs_word),
    .Byte_out(isolator_2_3_1_byte_out), .Link_in(decode_1_link), .Link_out(isolator_2_3_1_link_out),
    .Jump_in(disable_jump_1_jump_out), .Jump_out(isolator_2_3_1_jump_out), .SAsel_in(decode_1_sasel),
    .SAsel_out(isolator_2_3_1_sasel_out), .CompCode_in(decode_1_comp_code),
    .CompCode_out(isolator_2_3_1_compcode_out), .Branch_in(decode_1_branch_not_jump),
    .BranchnotJump_out(isolator_2_3_1_branchnotjump_out), .JR_out(isolator_2_3_1_jr_out),
    .JR_in(decode_1_r_type_jump), .Disable(and_1_out));
  and and_1 (and_1_out, execute_1_load_fwd, isolate34_1_wbmux_out);
  Execute execute_1 (
    .ALUcode(isolator_2_3_1_alu_out), .Out2(registerfile_1_p1), .WEin(isolator_2_3_1_wer_out),
    .Out1(linking_1_c_out), .SA(isolator_2_3_1_sa_out), .rd2(registerfile_1_p4), .rd1(linking_1_rd_out),
    .Immediate(isolator_2_3_1_imm_out), .ImmMux(isolator_2_3_1_immmux_out),
    .Signed(isolator_2_3_1_signed_out), .WER_out(execute_1_wer_out), .rt(isolator_2_3_1_rt_out),
    .rs(isolator_2_3_1_rs_out), .B(isolator_2_3_1_b_out), .A(isolator_2_3_1_a_out), .C_out(execute_1_c_out),
    .WE2(registerfile_1_p3), .WE1(isolate34_1_wer_out), .Jump_in(isolator_2_3_1_jump_out),
    .Jump_out(execute_1_jump_out), .Comp_Code(isolator_2_3_1_compcode_out), .PC_in(isolator_2_3_1_pc_out),
    .JR_in(isolator_2_3_1_jr_out), .Br_in(isolator_2_3_1_branchnotjump_out),
    .SAsel(isolator_2_3_1_sasel_out), .B_Out(execute_1_b_out), .Load_Fwd(execute_1_load_fwd));
  Disable_Load disable_load_1 (
    .WER_in(execute_1_wer_out), .WED_in(isolator_2_3_1_wed_out), .LoadStall(and_1_out),
    .Jump_in(execute_1_jump_out), .Mux2_in(isolator_2_3_1_wbmux_out), .WER_out(disable_load_1_wer_out),
    .WED_out(disable_load_1_wed_out), .Jump_out(disable_load_1_jump_out), .Mux2_out(disable_load_1_mux2_out));
  Isolate_45 isolate_45_1 (
    .C_in(multiplexer_2_out), .rd_in(linking_1_rd_out), .WER_in(isolate34_1_wer_out), .clock(clock_1_out),
    .C_out(registerfile_1_p1), .rd_out(registerfile_1_p4), .WER_out(registerfile_1_p3));
  Linking linking_1 (
    .rd_in(isolate34_1_rd_out), .Link_Enable(isolate34_1_link_out), .C_in(isolate34_1_c_out),
    .Link_Address(isolate34_1_linkaddress_out), .rd_out(linking_1_rd_out), .C_out(linking_1_c_out));
  Isolate34 isolate34_1 (
    .C_in(execute_1_c_out), .rd_in(isolator_2_3_1_rd_out), .WBMUX_in(disable_load_1_mux2_out),
    .WER_in(disable_load_1_wer_out), .WED_in(disable_load_1_wed_out), .clock(clock_1_out),
    .C_out(isolate34_1_c_out), .rd_out(isolate34_1_rd_out), .WBMUX_out(isolate34_1_wbmux_out),
    .WER_out(isolate34_1_wer_out), .WED_out(isolate34_1_wed_out), .Byte_in(isolator_2_3_1_byte_out),
    .Byte_out(isolate34_1_byte_out), .Link_in(isolator_2_3_1_link_out), .Link_out(isolate34_1_link_out),
    .Jump_Branch_in(disable_load_1_jump_out), .Jump_Branch_out(isolate34_1_jump_branch_out),
    .LinkAddress_in(register_1_q), .LinkAddress_out(isolate34_1_linkaddress_out), .Write_in(execute_1_b_out),
    .Write_out(isolate34_1_write_out), .Signed_in(isolator_2_3_1_signed_out),
    .Signed_out(isolate34_1_signed_out));
  Multiplexer #(.width(32), .enable("false")) multiplexer_2 (
    .in0(linking_1_c_out), .in1(byteextract_1_output), .out(multiplexer_2_out), .sel(isolate34_1_wbmux_out));
  ByteExtract byteextract_1 (
    .Signed(isolate34_1_signed_out), .ByteSelect(memoryhelp_1_sel), .Output(byteextract_1_output),
    .Input(mips_ram_1_p7), .Byte_Enable(isolate34_1_byte_out));
  MemoryHelp memoryhelp_1 (
    .C_in(isolate34_1_c_out), .Byte_in(isolate34_1_byte_out), .Write_in(isolate34_1_write_out),
    .A(memoryhelp_1_a), .Sel(memoryhelp_1_sel), .Write_Out(memoryhelp_1_write_out));
  // MIPS_RAM mips_ram_1: pin names not known; wires that end beside it: memoryhelp_1_a, memoryhelp_1_write_out, isolate34_1_wed_out, memoryhelp_1_sel, clock_1_out, isolate34_1_wbmux_out, mips_ram_1_p7

  // Notes on the sheet:
  //   Load Stall
  //   Jump
  //   Target Address
endmodule

module Count__1 (
  input  [31:0] PC,
  output [31:0] PC_4
);

  // Incrementer incrementer_1: pin names not known; wires that end beside it: PC[31:2], PC_4[31:2]

  assign PC_4[1:0] = PC[1:0];
endmodule

module Split (
  input  [31:0] Instr,
  output [5:0] Func,
  output [4:0] shamt,
  output [4:0] rd,
  output [15:0] Imm,
  output [4:0] rt,
  output [4:0] rs,
  output [25:0] InstrIndex,
  output [5:0] Op
);


  assign Func = Instr[5:0];
  assign Imm = Instr[15:0];
  assign InstrIndex = Instr[25:0];
  assign Op = Instr[31:26];
  assign rd = Instr[15:11];
  assign rs = Instr[25:21];
  assign rt = Instr[20:16];
  assign shamt = Instr[10:6];
endmodule

module Isolator_2_3 (
  input  [4:0] rs_in,
  input  [4:0] rt_in,
  input  [31:0] PC_in,
  input  [31:0] Imm_in,
  input  [31:0] A_in,
  input  [31:0] B_in,
  input  [4:0] rd_in,
  input  [4:0] sa_in,
  input  [3:0] ALU_in,
  input  ImmMux_in,
  input  WBMUX_in,
  input  WER_in,
  input  WED_in,
  input  Signed_in,
  input  Byte_in,
  input  Link_in,
  input  Jump_in,
  input  SAsel_in,
  input  [2:0] CompCode_in,
  input  Branch_in,
  input  JR_in,
  input  Disable,
  input  clock,
  output [4:0] rs_out,
  output [4:0] rt_out,
  output [31:0] PC_out,
  output [31:0] Imm_out,
  output [31:0] A_out,
  output [31:0] B_out,
  output [4:0] rd_out,
  output [4:0] sa_out,
  output [3:0] ALU_out,
  output ImmMux_out,
  output WBMUX_out,
  output WER_out,
  output WED_out,
  output Signed_out,
  output Byte_out,
  output Link_out,
  output Jump_out,
  output SAsel_out,
  output [2:0] CompCode_out,
  output BranchnotJump_out,
  output JR_out
);

  wire not_1_out;

  not not_1 (not_1_out, Disable);
  Register #(.width(5)) rs (.D(rs_in), .en(not_1_out), .Q(rs_out), .clk(clock));  // open: clr
  Register #(.width(5)) rt (.D(rt_in), .en(not_1_out), .Q(rt_out), .clk(clock));  // open: clr
  Register #(.width(32)) PC (.D(PC_in), .en(not_1_out), .Q(PC_out), .clk(clock));  // open: clr
  Register #(.width(32)) Imm (.D(Imm_in), .en(not_1_out), .Q(Imm_out), .clk(clock));  // open: clr
  Register #(.width(32)) A (.D(A_in), .en(not_1_out), .Q(A_out), .clk(clock));  // open: clr
  Register #(.width(32)) B (.D(B_in), .en(not_1_out), .Q(B_out), .clk(clock));  // open: clr
  Register #(.width(5)) rd (.D(rd_in), .en(not_1_out), .Q(rd_out), .clk(clock));  // open: clr
  Register #(.width(5)) sa (.D(sa_in), .en(not_1_out), .Q(sa_out), .clk(clock));  // open: clr
  Register #(.width(4)) aluop (.D(ALU_in), .en(not_1_out), .Q(ALU_out), .clk(clock));  // open: clr
  Register #(.width(1)) IE (.D(ImmMux_in), .en(not_1_out), .Q(ImmMux_out), .clk(clock));  // open: clr
  Register #(.width(1)) WBMUX (.D(WBMUX_in), .en(not_1_out), .Q(WBMUX_out), .clk(clock));  // open: clr
  Register #(.width(1)) WER (.D(WER_in), .Q(WER_out), .clk(clock));  // open: en, clr
  Register #(.width(1)) WED (.D(WED_in), .en(not_1_out), .Q(WED_out), .clk(clock));  // open: clr
  Register #(.width(1)) Signed (.D(Signed_in), .en(not_1_out), .Q(Signed_out), .clk(clock));  // open: clr
  Register #(.width(1)) Byte (.D(Byte_in), .en(not_1_out), .Q(Byte_out), .clk(clock));  // open: clr
  Register #(.width(1)) Link (.D(Link_in), .en(not_1_out), .Q(Link_out), .clk(clock));  // open: clr
  Register #(.width(1)) Jump (.D(Jump_in), .en(not_1_out), .Q(Jump_out), .clk(clock));  // open: clr
  Register #(.width(1)) SAsel (.D(SAsel_in), .en(not_1_out), .Q(SAsel_out), .clk(clock));  // open: clr
  Register #(.width(3)) CompCode (.D(CompCode_in), .en(not_1_out), .Q(CompCode_out), .clk(clock));  // open: clr
  Register #(.width(1)) Branch (.D(Branch_in), .en(not_1_out), .Q(BranchnotJump_out), .clk(clock));  // open: clr
  Register #(.width(1)) JR (.D(JR_in), .en(not_1_out), .Q(JR_out), .clk(clock));  // open: clr
endmodule

module Isolate34 (
  input  [31:0] Write_in,
  input  [31:0] C_in,
  input  [4:0] rd_in,
  input  WBMUX_in,
  input  WER_in,
  input  WED_in,
  input  clock,
  input  Byte_in,
  input  Link_in,
  input  Jump_Branch_in,
  input  [31:0] LinkAddress_in,
  input  Signed_in,
  output [31:0] Write_out,
  output [31:0] C_out,
  output [4:0] rd_out,
  output WBMUX_out,
  output WER_out,
  output WED_out,
  output Byte_out,
  output Link_out,
  output Jump_Branch_out,
  output [31:0] LinkAddress_out,
  output Signed_out
);

  Register #(.width(32)) Write (.D(Write_in), .Q(Write_out), .clk(clock));  // open: en, clr
  Register #(.width(32)) C (.D(C_in), .Q(C_out), .clk(clock));  // open: en, clr
  Register #(.width(5)) rd (.D(rd_in), .Q(rd_out), .clk(clock));  // open: en, clr
  Register #(.width(1)) WBMUX (.D(WBMUX_in), .Q(WBMUX_out), .clk(clock));  // open: en, clr
  Register #(.width(1)) WER (.D(WER_in), .Q(WER_out), .clk(clock));  // open: en, clr
  Register #(.width(1)) WED (.D(WED_in), .Q(WED_out), .clk(clock));  // open: en, clr
  Register #(.width(1)) Byte (.D(Byte_in), .Q(Byte_out), .clk(clock));  // open: en, clr
  Register #(.width(1)) Link (.D(Link_in), .Q(Link_out), .clk(clock));  // open: en, clr
  Register #(.width(1)) Jump_Branch (.D(Jump_Branch_in), .Q(Jump_Branch_out), .clk(clock));  // open: en, clr
  Register #(.width(32)) LinkAddress (.D(LinkAddress_in), .Q(LinkAddress_out), .clk(clock));  // open: en, clr
  Register #(.width(1)) Signed (.D(Signed_in), .Q(Signed_out), .clk(clock));  // open: en, clr
endmodule

module Isolate_45 (
  input  [31:0] C_in,
  input  [4:0] rd_in,
  input  WER_in,
  input  clock,
  output [31:0] C_out,
  output [4:0] rd_out,
  output WER_out
);

  Register #(.width(32)) C (.D(C_in), .Q(C_out), .clk(clock));  // open: en, clr
  Register #(.width(5)) rd (.D(rd_in), .Q(rd_out), .clk(clock));  // open: en, clr
  Register #(.width(1)) WER (.D(WER_in), .Q(WER_out), .clk(clock));  // open: en, clr
endmodule

module Forward (
  input  [31:0] Out0,
  input  WE1,
  input  [4:0] rd1,
  input  WE2,
  input  [4:0] rd2,
  input  [31:0] Out2,
  input  [31:0] Out1,
  input  [4:0] rs,
  output [31:0] Forwarded
);

  wire and_1_out, and_2_out, nor_1_out, nor_2_out, or_1_out;
  wire [4:0] xor_1_out, xor_2_out;
  wire [31:0] multiplexer_1_out;

  or or_1 (or_1_out, rs[0], rs[1], rs[2], rs[3], rs[4]);
  assign xor_1_out = rd1 ^ rs;  // XOR_Gate xor_1, 5 bits wide
  assign xor_2_out = rd2 ^ rs;  // XOR_Gate xor_2, 5 bits wide
  nor nor_1 (nor_1_out, xor_1_out[0], xor_1_out[1], xor_1_out[2], xor_1_out[3], xor_1_out[4]);
  nor nor_2 (nor_2_out, xor_2_out[0], xor_2_out[1], xor_2_out[2], xor_2_out[3], xor_2_out[4]);
  and and_1 (and_1_out, WE1, nor_1_out, or_1_out);
  Multiplexer #(.width(32), .enable("false")) multiplexer_1 (
    .in0(Out0), .in1(Out2), .out(multiplexer_1_out), .sel(and_2_out));
  and and_2 (and_2_out, WE2, nor_2_out, or_1_out);
  Multiplexer #(.width(32), .enable("false")) multiplexer_2 (
    .in0(multiplexer_1_out), .in1(Out1), .out(Forwarded), .sel(and_1_out));
endmodule

module Isolate12 (
  input  [31:0] PC_in,
  input  [31:0] Instr_in,
  input  Disable,
  input  clock,
  output [31:0] PC_out,
  output [31:0] Instr_out
);

  wire not_1_out;

  not not_1 (not_1_out, Disable);
  Register #(.width(32)) PC (.D(PC_in), .en(not_1_out), .Q(PC_out), .clk(clock));  // open: clr
  Register #(.width(32)) Instr (.D(Instr_in), .en(not_1_out), .Q(Instr_out), .clk(clock));  // open: clr
endmodule

module Decode (
  input  [5:0] Op,
  input  [4:0] rt,
  input  [5:0] Func,
  output SAsel,
  output [3:0] ALU_code,
  output MUX1,
  output MUX2,
  output WriteEnable1,
  output WriteEnable2,
  output Signed,
  output [1:0] Extend,
  output Load_Store_Byte_vs_Word,
  output Jump_Branch_Enable,
  output Link,
  output [2:0] Comp_Code,
  output Branch_not_Jump,
  output R_type_Jump
);

  wire i_j_out_1_branch_notjump, i_j_out_1_jump_branch_enable, i_j_out_1_link, i_j_out_1_mux1,
       i_j_out_1_mux2, i_j_out_1_sa, i_j_out_1_signed, i_j_out_1_we1, i_j_out_1_we2, nor_1_out,
       r_out_1_branch_not_jump, r_out_1_jump_branch_enable, r_out_1_link, r_out_1_mux1, r_out_1_mux2,
       r_out_1_sa, r_out_1_signed, r_out_1_we1, r_out_1_we2;
  wire [2:0] i_j_out_1_comp_code, r_out_1_comp_code;
  wire [3:0] i_j_out_1_o0, r_out_1_o0;

  nor nor_1 (nor_1_out, Op[0], Op[1], Op[2], Op[3], Op[4], Op[5]);
  I___J_Out i_j_out_1 (
    .B0(Op[0]), .B1(Op[1]), .B2(Op[2]), .B3(Op[3]), .B4(Op[4]), .B5(Op[5]), .rt_0(rt[0]),
    .O0(i_j_out_1_o0[0]), .O1(i_j_out_1_o0[1]), .O2(i_j_out_1_o0[2]), .O3(i_j_out_1_o0[3]),
    .MUX1(i_j_out_1_mux1), .MUX2(i_j_out_1_mux2), .SA(i_j_out_1_sa), .Signed(i_j_out_1_signed),
    .WE1(i_j_out_1_we1), .WE2(i_j_out_1_we2), .Extend(Extend[1]), .SL(Extend[0]),
    .L_S_Byte_or_Word(Load_Store_Byte_vs_Word), .Jump_Branch_Enable(i_j_out_1_jump_branch_enable),
    .Link(i_j_out_1_link), .Comp_Code(i_j_out_1_comp_code), .Branch_notjump(i_j_out_1_branch_notjump));
  R_Out r_out_1 (
    .B0(Func[0]), .B1(Func[1]), .B2(Func[2]), .B3(Func[3]), .B4(Func[4]), .B5(Func[5]), .rt_0(rt[0]),
    .O0(r_out_1_o0[0]), .O1(r_out_1_o0[1]), .O2(r_out_1_o0[2]), .O3(r_out_1_o0[3]), .MUX1(r_out_1_mux1),
    .MUX2(r_out_1_mux2), .SA(r_out_1_sa), .Signed(r_out_1_signed), .WE1(r_out_1_we1), .WE2(r_out_1_we2),
    .Jump_Branch_Enable(r_out_1_jump_branch_enable), .Link(r_out_1_link), .Comp_Code(r_out_1_comp_code),
    .Branch_not_Jump(r_out_1_branch_not_jump));
  Multiplexer #(.width(4), .enable("false")) multiplexer_1 (
    .in0(i_j_out_1_o0), .in1(r_out_1_o0), .out(ALU_code), .sel(nor_1_out));
  Multiplexer #(.enable("false")) multiplexer_2 (.in0(i_j_out_1_mux1), .in1(r_out_1_mux1), .out(MUX1), .sel(nor_1_out));
  Multiplexer #(.enable("false")) multiplexer_3 (.in0(i_j_out_1_mux2), .in1(r_out_1_mux2), .out(MUX2), .sel(nor_1_out));
  Multiplexer #(.enable("false")) multiplexer_4 (.in0(i_j_out_1_sa), .in1(r_out_1_sa), .out(SAsel), .sel(nor_1_out));
  Multiplexer #(.enable("false")) multiplexer_5 (
    .in0(i_j_out_1_signed), .in1(r_out_1_signed), .out(Signed), .sel(nor_1_out));
  Multiplexer #(.enable("false")) multiplexer_6 (
    .in0(i_j_out_1_we1), .in1(r_out_1_we1), .out(WriteEnable1), .sel(nor_1_out));
  Multiplexer #(.enable("false")) multiplexer_7 (
    .in0(i_j_out_1_we2), .in1(r_out_1_we2), .out(WriteEnable2), .sel(nor_1_out));
  Multiplexer #(.enable("false")) multiplexer_8 (
    .in0(i_j_out_1_jump_branch_enable), .in1(r_out_1_jump_branch_enable), .out(Jump_Branch_Enable),
    .sel(nor_1_out));
  Multiplexer #(.enable("false")) multiplexer_9 (.in0(i_j_out_1_link), .in1(r_out_1_link), .out(Link), .sel(nor_1_out));
  Multiplexer #(.width(3), .enable("false")) multiplexer_10 (
    .in0(i_j_out_1_comp_code), .in1(r_out_1_comp_code), .out(Comp_Code), .sel(nor_1_out));
  Multiplexer #(.enable("false")) multiplexer_11 (
    .in0(i_j_out_1_branch_notjump), .in1(r_out_1_branch_not_jump), .out(Branch_not_Jump), .sel(nor_1_out));
  and and_1 (R_type_Jump, Jump_Branch_Enable, nor_1_out);
endmodule

module I___J_Out (
  input  B0,
  input  B1,
  input  B2,
  input  B3,
  input  B4,
  input  B5,
  input  rt_0,
  output O0,
  output O1,
  output O2,
  output O3,
  output MUX1,
  output MUX2,
  output SA,
  output Signed,
  output WE1,
  output WE2,
  output Extend,
  output SL,
  output L_S_Byte_or_Word,
  output Jump_Branch_Enable,
  output Link,
  output [2:0] Comp_Code,
  output Branch_notjump
);

  wire and_1_out, and_2_out, and_3_out, and_4_out, and_5_out, and_6_out, and_7_out, and_8_out, and_10_out,
       and_12_out, and_13_out, and_14_out, and_15_out, and_16_out, and_17_out, and_18_out, and_19_out,
       and_20_out, and_21_out, and_22_out, and_23_out, and_24_out, and_25_out, and_26_out, and_27_out,
       and_28_out, and_29_out, and_30_out, and_31_out, and_32_out, and_33_out, and_34_out, and_35_out,
       and_36_out, and_37_out, and_38_out, and_39_out, and_40_out, and_41_out, and_42_out, and_43_out,
       and_44_out, and_45_out, and_46_out, and_47_out, and_48_out, and_50_out, and_51_out, and_52_out,
       and_53_out, and_54_out, and_55_out, and_56_out, and_57_out, and_58_out, and_59_out, and_60_out,
       and_61_out, and_62_out, and_64_out, and_65_out, and_67_out, and_68_out, and_69_out, and_73_out,
       nand_1_out, nand_2_out, nand_3_out, nor_1_out, not_1_out, not_2_out, not_3_out, not_4_out, not_5_out,
       not_6_out, not_7_out, not_8_out, not_9_out, not_10_out, not_11_out, not_12_out, not_13_out,
       not_14_out, not_15_out, not_16_out, not_17_out, not_18_out, not_19_out, not_20_out, not_21_out,
       not_22_out, not_23_out, not_24_out, not_25_out, not_26_out, not_27_out, not_28_out, not_29_out,
       not_30_out, not_31_out, not_32_out, not_33_out, not_34_out, not_35_out, not_36_out, not_37_out,
       not_38_out, not_39_out, not_40_out, not_41_out, not_42_out, not_43_out, not_44_out, not_45_out,
       not_46_out, not_47_out, not_48_out, not_49_out, not_50_out, not_51_out, not_52_out, not_53_out,
       not_54_out, not_55_out, not_56_out, not_57_out, not_58_out, not_59_out, not_60_out, not_61_out,
       not_62_out, not_63_out, not_64_out, not_65_out, not_66_out, not_67_out, not_68_out, not_69_out,
       not_70_out, not_71_out, not_72_out, not_73_out, not_74_out, not_75_out, not_76_out, not_77_out,
       not_78_out, not_79_out, not_80_out, not_81_out, not_82_out, not_83_out, not_84_out, not_85_out,
       not_86_out, not_87_out, not_88_out, not_89_out, not_90_out, not_91_out, not_92_out, not_93_out,
       not_94_out, not_95_out, not_96_out, not_97_out, not_98_out, not_99_out, not_100_out, not_101_out,
       not_102_out, not_103_out, not_104_out, not_105_out, not_106_out, not_107_out, not_108_out,
       not_109_out, not_110_out, not_111_out, not_112_out, not_113_out, not_114_out, not_115_out,
       not_116_out, not_117_out, not_118_out, not_119_out, not_120_out, or_1_out, or_2_out, or_3_out,
       or_4_out, or_5_out, or_6_out, or_7_out, or_8_out, or_9_out, or_10_out, or_11_out, xnor_1_out,
       xnor_2_out, xnor_3_out, xnor_4_out, xnor_5_out, xnor_6_out, xnor_7_out;

  not not_1 (not_1_out, B5);
  not not_2 (not_2_out, B4);
  not not_3 (not_3_out, B2);
  not not_4 (not_4_out, B1);
  not not_5 (not_5_out, B2);
  not not_6 (not_6_out, B5);
  and and_1 (and_1_out, not_6_out, not_7_out, not_8_out);
  not not_7 (not_7_out, B4);
  not not_8 (not_8_out, B3);
  not not_9 (not_9_out, B4);
  not not_10 (not_10_out, B2);
  not not_11 (not_11_out, B0);
  not not_12 (not_12_out, B2);
  not not_13 (not_13_out, B2);
  not not_14 (not_14_out, B1);
  not not_15 (not_15_out, B5);
  and and_2 (and_2_out, not_15_out, not_16_out, not_17_out);
  not not_16 (not_16_out, B4);
  not not_17 (not_17_out, B3);
  not not_18 (not_18_out, B4);
  not not_19 (not_19_out, B2);
  not not_20 (not_20_out, B5);
  not not_21 (not_21_out, B4);
  and and_3 (and_3_out, B5, not_22_out, not_23_out);
  not not_22 (not_22_out, B4);
  not not_23 (not_23_out, B3);
  and and_4 (and_4_out, B2, not_24_out, not_25_out);
  not not_24 (not_24_out, B1);
  not not_25 (not_25_out, B0);
  not not_26 (not_26_out, B2);
  not not_27 (not_27_out, B5);
  not not_28 (not_28_out, B4);
  not not_29 (not_29_out, B2);
  not not_30 (not_30_out, B0);
  not not_31 (not_31_out, B4);
  not not_32 (not_32_out, B2);
  not not_33 (not_33_out, B5);
  not not_34 (not_34_out, B4);
  not not_35 (not_35_out, B2);
  not not_36 (not_36_out, B1);
  not not_37 (not_37_out, B0);
  not not_38 (not_38_out, B5);
  and and_5 (and_5_out, not_38_out, not_39_out, not_40_out);
  not not_39 (not_39_out, B4);
  not not_40 (not_40_out, B3);
  not not_41 (not_41_out, B2);
  and and_6 (and_6_out, not_41_out, B1, B0);
  not not_42 (not_42_out, B4);
  and and_7 (and_7_out, B5, not_42_out, not_43_out);
  not not_43 (not_43_out, B3);
  and and_8 (and_8_out, B2, not_44_out, not_45_out);
  not not_44 (not_44_out, B1);
  not not_45 (not_45_out, B0);
  not not_46 (not_46_out, B2);
  not not_47 (not_47_out, B4);
  not not_48 (not_48_out, B2);
  not not_49 (not_49_out, B2);
  not not_50 (not_50_out, B1);
  not not_51 (not_51_out, B2);
  not not_52 (not_52_out, B4);
  not not_53 (not_53_out, B2);
  not not_54 (not_54_out, B4);
  not not_55 (not_55_out, B3);
  not not_56 (not_56_out, B1);
  not not_57 (not_57_out, B0);
  not not_58 (not_58_out, B5);
  not not_59 (not_59_out, B4);
  not not_60 (not_60_out, B3);
  not not_61 (not_61_out, B2);
  not not_62 (not_62_out, B5);
  not not_63 (not_63_out, B4);
  not not_64 (not_64_out, B3);
  not not_65 (not_65_out, B2);
  not not_66 (not_66_out, B5);
  not not_67 (not_67_out, B4);
  not not_68 (not_68_out, B4);
  not not_69 (not_69_out, B3);
  not not_70 (not_70_out, B1);
  not not_71 (not_71_out, B0);
  not not_72 (not_72_out, B4);
  not not_73 (not_73_out, B2);
  not not_74 (not_74_out, B1);
  not not_75 (not_75_out, B0);
  not not_76 (not_76_out, B5);
  and and_9 (Jump_Branch_Enable, not_76_out, not_77_out, not_78_out);
  not not_77 (not_77_out, B4);
  not not_78 (not_78_out, B3);
  not not_79 (not_79_out, B2);
  and and_10 (and_10_out, not_79_out, B1, B0);
  not not_80 (not_80_out, B5);
  not not_81 (not_81_out, B4);
  not not_82 (not_82_out, B3);
  not not_83 (not_83_out, B2);
  not not_84 (not_84_out, B1);
  not not_85 (not_85_out, rt_0);
  not not_86 (not_86_out, B1);
  not not_87 (not_87_out, B5);
  not not_88 (not_88_out, B4);
  not not_89 (not_89_out, B2);
  not not_90 (not_90_out, B5);
  not not_91 (not_91_out, B4);
  not not_92 (not_92_out, B3);
  not not_93 (not_93_out, B1);
  not not_94 (not_94_out, B2);
  not not_95 (not_95_out, B1);
  not not_96 (not_96_out, B5);
  not not_97 (not_97_out, B4);
  not not_98 (not_98_out, B3);
  not not_99 (not_99_out, B2);
  not not_100 (not_100_out, B1);
  not not_101 (not_101_out, B5);
  not not_102 (not_102_out, B4);
  not not_103 (not_103_out, B3);
  not not_104 (not_104_out, B2);
  and and_11 (O0, not_1_out, not_2_out, B3, not_3_out, B1);
  and and_12 (and_12_out, not_4_out, B0);
  and and_13 (and_13_out, not_5_out, B1);
  and and_14 (and_14_out, B2, B1, B0);
  and and_15 (and_15_out, B5, not_9_out);
  and and_16 (and_16_out, and_15_out, and_17_out);
  and and_17 (and_17_out, not_10_out, xnor_1_out);
  xnor xnor_1 (xnor_1_out, B1, B0);
  not not_105 (not_105_out, B4);
  not not_106 (not_106_out, B3);
  and and_18 (and_18_out, B5, not_105_out, not_106_out, B2, not_107_out, not_108_out);
  not not_107 (not_107_out, B1);
  not not_108 (not_108_out, B0);
  and and_19 (and_19_out, B2, B1, not_11_out);
  and and_20 (and_20_out, not_12_out, B1);
  and and_21 (and_21_out, not_13_out, not_14_out, B0);
  and and_22 (and_22_out, B2, B1, B0);
  and and_23 (and_23_out, B5, not_18_out);
  and and_24 (and_24_out, and_23_out, and_25_out);
  and and_25 (and_25_out, not_19_out, xnor_2_out);
  xnor xnor_2 (xnor_2_out, B1, B0);
  not not_109 (not_109_out, B4);
  not not_110 (not_110_out, B3);
  and and_26 (and_26_out, B5, not_109_out, not_110_out, B2, not_111_out, not_112_out);
  not not_111 (not_111_out, B1);
  not not_112 (not_112_out, B0);
  and and_27 (and_27_out, not_20_out, not_21_out, B3);
  or or_1 (or_1_out, and_4_out, and_28_out);
  and and_28 (and_28_out, not_26_out, xnor_3_out);
  xnor xnor_3 (xnor_3_out, B1, B0);
  and and_29 (and_29_out, not_27_out, not_28_out, B3, not_29_out, B1, not_30_out);
  and and_30 (and_30_out, B5, not_31_out);
  and and_31 (and_31_out, and_30_out, and_32_out);
  and and_32 (and_32_out, not_32_out, xnor_4_out);
  xnor xnor_4 (xnor_4_out, B1, B0);
  and and_33 (and_33_out, not_33_out, not_34_out, B3);
  nand nand_1 (nand_1_out, not_35_out, not_36_out, not_37_out);
  and and_34 (and_34_out, and_5_out, and_6_out);
  or or_2 (or_2_out, and_8_out, and_35_out);
  and and_35 (and_35_out, not_46_out, xnor_5_out);
  xnor xnor_5 (xnor_5_out, B1, B0);
  xnor xnor_6 (xnor_6_out, B1, B0);
  not not_113 (not_113_out, B5);
  not not_114 (not_114_out, B4);
  and and_36 (and_36_out, not_113_out, not_114_out, B3);
  and and_37 (and_37_out, not_49_out, not_50_out, B0);
  or or_3 (or_3_out, and_37_out, and_38_out);
  and and_38 (and_38_out, not_51_out, B1);
  and and_39 (and_39_out, B5, not_52_out, not_53_out);
  and and_40 (and_40_out, and_39_out, xnor_7_out);
  xnor xnor_7 (xnor_7_out, B1, B0);
  and and_41 (and_41_out, B5, not_54_out, not_55_out);
  and and_42 (and_42_out, and_41_out, and_43_out);
  and and_43 (and_43_out, B2, not_56_out, not_57_out);
  and and_44 (and_44_out, not_58_out, not_59_out, not_60_out);
  nand nand_2 (nand_2_out, not_61_out, B1);
  and and_45 (and_45_out, not_62_out, not_63_out, not_64_out, not_65_out, B1);
  and and_46 (and_46_out, not_66_out, not_67_out, B3, B2, B1, B0);
  and and_47 (and_47_out, B5, not_68_out, not_69_out, B2, not_70_out, not_71_out);
  and and_48 (and_48_out, B5, not_72_out, not_73_out, not_74_out, not_75_out);
  and and_49 (Link, Jump_Branch_Enable, and_10_out);
  and and_50 (and_50_out, not_80_out, not_81_out, not_82_out);
  and and_51 (and_51_out, B2, B1, B0);
  and and_52 (and_52_out, not_83_out, not_84_out, B0, not_85_out);
  and and_53 (and_53_out, B2, not_86_out, B0);
  and and_54 (and_54_out, not_87_out, not_88_out, B3, not_89_out, B1);
  and and_55 (and_55_out, not_90_out, not_91_out, not_92_out);
  and and_56 (and_56_out, B2, not_93_out);
  and and_57 (and_57_out, B2, B1, B0);
  and and_58 (and_58_out, not_94_out, not_95_out, B0, rt_0);
  and and_59 (and_59_out, not_96_out, not_97_out, not_98_out);
  and and_60 (and_60_out, not_99_out, not_100_out, B0);
  or or_4 (or_4_out, and_60_out, and_61_out);
  and and_61 (and_61_out, B2, B1);
  and and_62 (and_62_out, not_101_out, not_102_out, not_103_out);
  nand nand_3 (nand_3_out, not_104_out, B1);
  not not_115 (not_115_out, B5);
  not not_116 (not_116_out, B4);
  or or_5 (or_5_out, and_12_out, and_13_out, and_14_out);
  or or_6 (or_6_out, and_16_out, and_18_out);
  not not_117 (not_117_out, B5);
  not not_118 (not_118_out, B4);
  or or_7 (or_7_out, and_19_out, and_20_out);
  not not_119 (not_119_out, B5);
  not not_120 (not_120_out, B4);
  nor nor_1 (nor_1_out, and_21_out, and_22_out);
  or or_8 (or_8_out, and_24_out, and_26_out);
  and and_63 (MUX2, and_3_out, or_1_out);
  and and_64 (and_64_out, and_33_out, nand_1_out);
  and and_65 (and_65_out, and_7_out, or_2_out);
  and and_66 (WE2, B5, not_47_out, B3, not_48_out, xnor_6_out);
  and and_67 (and_67_out, and_36_out, or_3_out);
  or or_9 (or_9_out, and_40_out, and_42_out);
  and and_68 (and_68_out, and_44_out, nand_2_out);
  and and_69 (and_69_out, and_50_out, or_10_out);
  or or_10 (or_10_out, and_51_out, and_52_out, and_53_out);
  and and_70 (Comp_Code[1], and_55_out, or_11_out);
  or or_11 (or_11_out, and_56_out, and_57_out, and_58_out);
  and and_71 (Comp_Code[2], and_59_out, or_4_out);
  and and_72 (Branch_notjump, and_62_out, nand_3_out);
  and and_73 (and_73_out, not_115_out, not_116_out, B3, or_5_out);
  or or_12 (O1, and_73_out, and_1_out, or_6_out);
  and and_74 (O2, not_117_out, not_118_out, B3, or_7_out);
  and and_75 (O3, not_119_out, not_120_out, B3, nor_1_out);
  or or_13 (MUX1, and_2_out, or_8_out, and_27_out);
  or or_14 (Signed, and_29_out, and_31_out);
  or or_15 (WE1, and_64_out, and_34_out, and_65_out);
  or or_16 (Extend, and_67_out, or_9_out, and_68_out);
  or or_17 (SL, and_45_out, and_46_out);
  or or_18 (L_S_Byte_or_Word, and_47_out, and_48_out);
  or or_19 (Comp_Code[0], and_69_out, and_54_out);

  assign SA = 1'b1;
endmodule

module R_Out (
  input  B0,
  input  B1,
  input  B2,
  input  B3,
  input  B4,
  input  B5,
  input  rt_0,
  output O0,
  output O1,
  output O2,
  output O3,
  output MUX1,
  output MUX2,
  output SA,
  output Signed,
  output WE1,
  output WE2,
  output Jump_Branch_Enable,
  output Link,
  output [2:0] Comp_Code,
  output Branch_not_Jump
);

  wire and_1_out, and_2_out, and_3_out, and_4_out, and_5_out, and_6_out, and_7_out, and_8_out, and_9_out,
       and_10_out, and_11_out, and_12_out, and_14_out, and_15_out, and_16_out, and_17_out, and_18_out,
       and_19_out, and_22_out, and_25_out, and_26_out, and_27_out, and_28_out, and_29_out, nand_1_out,
       nand_2_out, not_1_out, not_2_out, not_3_out, not_4_out, not_5_out, not_6_out, not_7_out, not_8_out,
       not_9_out, not_10_out, not_11_out, not_12_out, not_13_out, not_14_out, not_15_out, not_16_out,
       not_17_out, not_18_out, not_19_out, not_20_out, not_21_out, not_22_out, not_23_out, not_24_out,
       not_25_out, not_26_out, not_27_out, not_28_out, not_29_out, not_30_out, not_31_out, not_32_out,
       not_33_out, not_34_out, not_35_out, not_36_out, not_37_out, not_38_out, not_39_out, not_40_out,
       not_41_out, not_42_out, not_43_out, not_44_out, not_45_out, not_46_out, not_47_out, not_48_out,
       not_49_out, not_50_out, not_51_out, not_52_out, not_53_out, not_54_out, not_55_out, not_56_out,
       or_1_out, or_3_out, or_4_out;

  not not_1 (not_1_out, B4);
  not not_2 (not_2_out, B2);
  not not_3 (not_3_out, B5);
  not not_4 (not_4_out, B4);
  not not_5 (not_5_out, B2);
  not not_6 (not_6_out, B5);
  not not_7 (not_7_out, B4);
  not not_8 (not_8_out, B3);
  not not_9 (not_9_out, B2);
  not not_10 (not_10_out, B1);
  not not_11 (not_11_out, B2);
  not not_12 (not_12_out, B1);
  not not_13 (not_13_out, B2);
  not not_14 (not_14_out, B4);
  not not_15 (not_15_out, B3);
  not not_16 (not_16_out, B4);
  not not_17 (not_17_out, B2);
  not not_18 (not_18_out, B1);
  not not_19 (not_19_out, B4);
  not not_20 (not_20_out, B2);
  not not_21 (not_21_out, B0);
  not not_22 (not_22_out, B4);
  not not_23 (not_23_out, B2);
  not not_24 (not_24_out, B4);
  not not_25 (not_25_out, B3);
  not not_26 (not_26_out, B5);
  not not_27 (not_27_out, B4);
  not not_28 (not_28_out, B3);
  not not_29 (not_29_out, B1);
  not not_30 (not_30_out, B5);
  not not_31 (not_31_out, B4);
  not not_32 (not_32_out, B2);
  not not_33 (not_33_out, B1);
  not not_34 (not_34_out, B5);
  not not_35 (not_35_out, B4);
  not not_36 (not_36_out, B2);
  not not_37 (not_37_out, B1);
  and and_1 (and_1_out, B5, not_1_out, B3, not_2_out, B1);
  and and_2 (and_2_out, not_3_out, not_4_out, B3, not_5_out, B1);
  and and_3 (and_3_out, not_6_out, not_7_out, not_8_out, B1, B0);
  and and_4 (and_4_out, not_9_out, not_10_out, B0);
  and and_5 (and_5_out, not_11_out, B1, B0);
  and and_6 (and_6_out, B2, not_12_out, B0);
  and and_7 (and_7_out, B2, B1, B0);
  not not_38 (not_38_out, B5);
  and and_8 (and_8_out, not_38_out, not_39_out);
  not not_39 (not_39_out, B0);
  and and_9 (and_9_out, not_13_out, B1, B0);
  and and_10 (and_10_out, B2, B1);
  and and_11 (and_11_out, B5, not_14_out, not_15_out, B2);
  and and_12 (and_12_out, not_16_out, B3, not_17_out, B1);
  not not_40 (not_40_out, B5);
  not not_41 (not_41_out, B4);
  not not_42 (not_42_out, B3);
  nand nand_1 (nand_1_out, not_18_out, B0);
  and and_13 (Signed, B5, not_19_out, B3, not_20_out, B1, not_21_out);
  and and_14 (and_14_out, not_22_out, B3, not_23_out, B1);
  and and_15 (and_15_out, B5, not_24_out, not_25_out);
  and and_16 (and_16_out, and_15_out, or_1_out);
  or or_1 (or_1_out, B2, B0);
  and and_17 (and_17_out, not_26_out, not_27_out, not_28_out);
  and and_18 (and_18_out, and_17_out, nand_2_out);
  nand nand_2 (nand_2_out, not_29_out, B0);
  and and_19 (and_19_out, not_30_out, not_31_out, B3, not_32_out, not_33_out);
  and and_20 (Jump_Branch_Enable, not_34_out, not_35_out, B3, not_36_out, not_37_out);
  not not_43 (not_43_out, B4);
  not not_44 (not_44_out, B2);
  or or_2 (O0, and_1_out, and_2_out, and_3_out);
  not not_45 (not_45_out, B4);
  not not_46 (not_46_out, B3);
  or or_3 (or_3_out, and_4_out, and_5_out, and_6_out, and_7_out);
  not not_47 (not_47_out, and_8_out);
  not not_48 (not_48_out, B4);
  not not_49 (not_49_out, B2);
  not not_50 (not_50_out, B4);
  not not_51 (not_51_out, B3);
  or or_4 (or_4_out, and_9_out, and_10_out);
  not not_52 (not_52_out, B4);
  not not_53 (not_53_out, B2);
  not not_54 (not_54_out, B5);
  not not_55 (not_55_out, B4);
  not not_56 (not_56_out, B3);
  or or_5 (O3, and_11_out, and_12_out);
  and and_21 (SA, not_40_out, not_41_out, not_42_out, B2, nand_1_out);
  and and_22 (and_22_out, and_19_out, B0);
  and and_23 (Link, Jump_Branch_Enable, B0);
  and and_24 (Comp_Code[0], B5, not_43_out, B3, not_44_out, B1);
  and and_25 (and_25_out, B5, not_45_out, not_46_out, or_3_out);
  and and_26 (and_26_out, not_47_out, not_48_out, B3, not_49_out, B1);
  and and_27 (and_27_out, B5, not_50_out, not_51_out, or_4_out);
  and and_28 (and_28_out, B5, not_52_out, B3, not_53_out, B1);
  and and_29 (and_29_out, not_54_out, not_55_out, not_56_out, B1);
  or or_6 (O1, and_25_out, and_26_out);
  or or_7 (O2, and_27_out, and_28_out, and_29_out);
  or or_8 (WE1, and_14_out, and_16_out, and_18_out, and_22_out);

  assign Branch_not_Jump = 1'b0;
  assign Comp_Code[2:1] = 2'b00;
  assign MUX1 = 1'b0;
  assign MUX2 = 1'b0;
  assign WE2 = 1'b0;
endmodule

module SAVar (
  input  [4:0] SA_in,
  input  [31:0] A_in,
  input  Select,
  output [4:0] SA_out
);

  Multiplexer #(.width(5)) multiplexer_1 (.in0(SA_in), .in1(A_in[4:0]), .out(SA_out), .sel(Select));  // open: en
endmodule

module BitExtend (
  input  [1:0] BitEx,
  input  Jump,
  input  [15:0] Imm_In,
  input  [25:0] InstrIndex,
  output [31:0] Imm_Out
);

  wire multiplexer_1_out;
  wire [31:0] bit_extender_1_out, bit_extender_2_out, multiplexer_2_out, multiplexer_3_out;

  Multiplexer #(.enable("false")) multiplexer_1 (.in0(1'b0), .in1(Imm_In[15]), .out(multiplexer_1_out), .sel(BitEx[1]));
  assign bit_extender_1_out = {{16{multiplexer_1_out}}, Imm_In};  // Bit_Extender bit_extender_1
  assign bit_extender_2_out = {{14{Imm_In[15]}}, {Imm_In, 2'b00}};  // Bit_Extender bit_extender_2
  Multiplexer #(.width(32), .enable("false")) multiplexer_2 (
    .in0(bit_extender_1_out), .in1({Imm_In, {16{1'b0}}}), .out(multiplexer_2_out), .sel(BitEx[0]));
  Multiplexer #(.width(32), .enable("false")) multiplexer_3 (
    .in0(bit_extender_2_out), .in1({4'b0000, InstrIndex, 2'b00}), .out(multiplexer_3_out), .sel(BitEx[0]));
  Multiplexer #(.width(32), .enable("false")) multiplexer_4 (
    .in0(multiplexer_2_out), .in1(multiplexer_3_out), .out(Imm_Out), .sel(Jump));
endmodule

module Execute (
  input  [3:0] ALUcode,
  input  [31:0] Out2,
  input  WEin,
  input  [31:0] Out1,
  input  [4:0] rd2,
  input  [4:0] rd1,
  input  [31:0] PC_in,
  input  WE2,
  input  [4:0] rt,
  input  [4:0] rs,
  input  WE1,
  input  [31:0] B,
  input  [31:0] A,
  input  [31:0] Immediate,
  input  ImmMux,
  input  [4:0] SA,
  input  SAsel,
  input  Signed,
  input  [2:0] Comp_Code,
  input  Br_in,
  input  JR_in,
  input  Jump_in,
  output WER_out,
  output Load_Fwd,
  output [31:0] C_out,
  output Jump_out,
  output [31:0] B_Out
);

  wire and_2_out, and_3_out, compare_1_compare_out, nand_1_out, not_1_out, not_2_out, not_3_out, not_4_out,
       or_1_out;
  wire [4:0] mips_alu_1_p4;
  wire [31:0] and_1_out, bit_extender_1_out, bit_extender_2_out, count_1_1_pc_4, forward_2_forwarded,
       mips_alu_1_p5, multiplexer_1_out, multiplexer_2_out, multiplexer_3_out, multiplexer_4_out,
       multiplexer_5_out;

  Forward forward_1 (
    .Out2(Out2), .rd2(rd2), .WE1(WE1), .rd1(rd1), .Out1(Out1), .WE2(WE2), .rs(rt), .Out0(B), .Forwarded(B_Out));
  not not_1 (not_1_out, ImmMux);
  or or_1 (or_1_out, not_1_out, Br_in);
  Multiplexer #(.width(32), .enable("false")) multiplexer_1 (
    .in0(B_Out), .in1(Immediate), .out(multiplexer_1_out), .sel(ImmMux));
  Multiplexer #(.width(32), .enable("false")) multiplexer_2 (
    .in0(Immediate), .in1(B_Out), .out(multiplexer_2_out), .sel(or_1_out));
  Forward forward_2 (
    .Out2(Out2), .rd2(rd2), .WE1(WE1), .rd1(rd1), .Out1(Out1), .WE2(WE2), .rs(rs), .Out0(A),
    .Forwarded(forward_2_forwarded));
  rsrt_equals_rd rsrt_equals_rd_1 (.rs(rs), .rd(rd1), .rt(rt), .Load_Forward(Load_Fwd));
  Count__1 count_1_1 (.PC(PC_in), .PC_4(count_1_1_pc_4));
  Multiplexer #(.width(32), .enable("false")) multiplexer_3 (
    .in0(forward_2_forwarded), .in1(count_1_1_pc_4), .out(multiplexer_3_out), .sel(Jump_in));
  assign and_1_out = bit_extender_1_out & multiplexer_3_out;  // AND_Gate and_1, 32 bits wide
  not not_2 (not_2_out, ALUcode[2]);
  not not_3 (not_3_out, and_3_out);
  // Mips_ALU mips_alu_1: pin names not known; wires that end beside it: and_1_out, multiplexer_1_out, ALUcode, mips_alu_1_p4, mips_alu_1_p5
  SAVar savar_1 (.Select(SAsel), .SA_in(SA), .A_in(forward_2_forwarded), .SA_out(mips_alu_1_p4));
  Compare compare_1 (
    .A(forward_2_forwarded), .B(multiplexer_2_out), .CompCode(Comp_Code),
    .Compare_Out(compare_1_compare_out), .Signed(Signed), .Branch(Br_in));
  and and_2 (and_2_out, ALUcode[0], ALUcode[1], ALUcode[2], ALUcode[3]);
  and and_3 (and_3_out, ALUcode[0], not_2_out, ALUcode[3]);
  assign bit_extender_1_out = {{31{not_3_out}}, not_3_out};  // Bit_Extender bit_extender_1
  assign bit_extender_2_out = {{31{1'b0}}, compare_1_compare_out};  // Bit_Extender bit_extender_2
  and and_4 (Jump_out, compare_1_compare_out, Jump_in);
  not not_4 (not_4_out, mips_alu_1_p5[0]);
  Multiplexer #(.width(32), .enable("false")) multiplexer_4 (
    .in0(mips_alu_1_p5), .in1(forward_2_forwarded), .out(multiplexer_4_out), .sel(and_3_out));
  nand nand_1 (nand_1_out, and_3_out, not_4_out);
  and and_5 (WER_out, nand_1_out, WEin);
  Multiplexer #(.width(32), .enable("false")) multiplexer_5 (
    .in0(multiplexer_4_out), .in1(bit_extender_2_out), .out(multiplexer_5_out), .sel(and_2_out));
  JumpAddress jumpaddress_1 (
    .Register_in(JR_in), .Branch_in(Br_in), .InstrIndex(multiplexer_1_out), .C_in(multiplexer_5_out),
    .PC_in(count_1_1_pc_4), .A_in(forward_2_forwarded), .PC_out(C_out), .Jump(Jump_in));
endmodule

module Compare (
  input  Signed,
  input  Branch,
  input  [31:0] A,
  input  [31:0] B,
  input  [2:0] CompCode,
  output Compare_Out
);

  wire and_1_out, and_3_out, and_4_out, and_5_out, and_6_out, and_7_out, and_8_out, and_9_out, and_10_out,
       and_11_out, and_12_out, and_13_out, comparator_1_lt, comparator_2_eq, comparator_2_gt,
       comparator_2_lt, multiplexer_1_out, nor_1_out, not_1_out, not_2_out, not_3_out, not_4_out, not_5_out,
       not_6_out, not_7_out, not_8_out, not_9_out, not_10_out, not_11_out, or_1_out, or_2_out;
  wire [31:0] and_2_out, bit_extender_1_out;

  not not_1 (not_1_out, CompCode[2]);
  assign bit_extender_1_out = {{31{not_1_out}}, not_1_out};  // Bit_Extender bit_extender_1
  and and_1 (and_1_out, CompCode[2], CompCode[1], CompCode[0]);
  assign and_2_out = B & bit_extender_1_out;  // AND_Gate and_2, 32 bits wide
  and and_3 (and_3_out, CompCode[2], CompCode[1], not_2_out);
  not not_2 (not_2_out, CompCode[0]);
  not not_3 (not_3_out, CompCode[1]);
  Comparator #(.width(32), .mode("unsigned")) comparator_1 (
    .a(A), .b(and_2_out), .lt(comparator_1_lt));  // open: gt, eq
  Comparator #(.width(32)) comparator_2 (
    .a(A), .b(and_2_out), .gt(comparator_2_gt), .eq(comparator_2_eq), .lt(comparator_2_lt));
  and and_4 (and_4_out, comparator_2_gt, and_1_out);
  and and_5 (and_5_out, not_3_out, CompCode[0]);
  not not_4 (not_4_out, comparator_2_lt);
  and and_6 (and_6_out, not_4_out, and_3_out);
  and and_7 (and_7_out, CompCode[2], not_5_out, not_6_out);
  not not_5 (not_5_out, CompCode[1]);
  not not_6 (not_6_out, CompCode[0]);
  not not_7 (not_7_out, comparator_2_gt);
  and and_8 (and_8_out, comparator_2_lt, and_5_out);
  not not_8 (not_8_out, CompCode[2]);
  and and_9 (and_9_out, not_8_out, CompCode[1], not_9_out);
  not not_9 (not_9_out, CompCode[0]);
  and and_10 (and_10_out, not_7_out, and_7_out);
  not not_10 (not_10_out, CompCode[2]);
  not not_11 (not_11_out, comparator_2_eq);
  and and_11 (and_11_out, not_11_out, and_13_out);
  and and_12 (and_12_out, comparator_2_eq, and_9_out);
  and and_13 (and_13_out, not_10_out, CompCode[1], CompCode[0]);
  nor nor_1 (nor_1_out, CompCode[0], CompCode[1], CompCode[2]);
  or or_1 (or_1_out, Signed, Branch);
  or or_2 (or_2_out, and_11_out, and_12_out, and_10_out, and_8_out, and_6_out, and_4_out);
  Multiplexer #(.enable("false")) multiplexer_1 (
    .in0(comparator_1_lt), .in1(or_2_out), .out(multiplexer_1_out), .sel(or_1_out));
  or or_3 (Compare_Out, multiplexer_1_out, nor_1_out);

  // Notes on the sheet:
  //   GT
  //   GE
  //   LT
  //   LE
  //   EQ
  //   NE
endmodule

module MemoryHelp (
  input  [31:0] C_in,
  input  Byte_in,
  input  [31:0] Write_in,
  output [19:0] A,
  output [3:0] Sel,
  output [31:0] Write_Out
);

  wire not_1_out;
  wire [3:0] and_1_out, bit_extender_1_out;

  Multiplexer #(.width(32), .enable("false")) multiplexer_1 (
    .in0(Write_in), .in1({Write_in[7:0], Write_in[7:0], Write_in[7:0], Write_in[7:0]}), .out(Write_Out),
    .sel(Byte_in));
  assign bit_extender_1_out = {{3{not_1_out}}, not_1_out};  // Bit_Extender bit_extender_1
  not not_1 (not_1_out, Byte_in);
  and and_1 (and_1_out[0], ~C_in[1], ~C_in[0]);  // AND_Gate
  and and_2 (and_1_out[1], ~C_in[1], C_in[0]);  // AND_Gate
  and and_3 (and_1_out[2], C_in[1], ~C_in[0]);  // AND_Gate
  and and_4 (and_1_out[3], C_in[1], C_in[0]);
  assign Sel = bit_extender_1_out | and_1_out;  // OR_Gate or_1, 4 bits wide

  assign A = C_in[21:2];
endmodule

module Disable_Jump (
  input  WER_in,
  input  WED_in,
  input  Jump,
  input  Jump_in,
  input  Mux2_in,
  output WER_out,
  output WED_out,
  output Jump_out,
  output Mux2_out
);

  wire not_1_out, not_2_out;

  not not_1 (not_1_out, Jump);
  not not_2 (not_2_out, Jump);
  and and_1 (WER_out, WER_in, not_1_out);
  and and_2 (WED_out, not_1_out, WED_in);
  and and_3 (Jump_out, Jump_in, not_2_out);
  and and_4 (Mux2_out, not_2_out, Mux2_in);
endmodule

module BranchMux (
  input  Jump_Branch,
  input  [31:0] PC_4,
  input  [31:0] JumpAddress,
  output [31:0] NewPC
);

  wire and_1_out, or_1_out;

  or or_1 (or_1_out, PC_4[31], PC_4[30], PC_4[29], PC_4[28], PC_4[27], PC_4[26], PC_4[25], PC_4[24], PC_4[23], PC_4[22], PC_4[21], PC_4[20], PC_4[19], PC_4[18], PC_4[17], PC_4[16], PC_4[15], PC_4[14], PC_4[13], PC_4[12], PC_4[11], PC_4[10], PC_4[9], PC_4[8], PC_4[7], PC_4[6], PC_4[5], PC_4[4], PC_4[3]);
  and and_1 (and_1_out, Jump_Branch, or_1_out);
  Multiplexer #(.width(32), .enable("false")) multiplexer_1 (
    .in0(PC_4), .in1(JumpAddress), .out(NewPC), .sel(and_1_out));
endmodule

module JumpAddress (
  input  Branch_in,
  input  Jump,
  input  Register_in,
  input  [31:0] C_in,
  input  [31:0] InstrIndex,
  input  [31:0] PC_in,
  input  [31:0] A_in,
  output [31:0] PC_out
);

  wire and_1_out, not_1_out;
  wire [31:0] multiplexer_1_out;

  not not_1 (not_1_out, Branch_in);
  and and_1 (and_1_out, not_1_out, Jump);
  Multiplexer #(.width(32), .enable("false")) multiplexer_1 (
    .in0(C_in), .in1({PC_in[31:28], InstrIndex[27:0]}), .out(multiplexer_1_out), .sel(and_1_out));
  Multiplexer #(.width(32), .enable("false")) multiplexer_2 (
    .in0(multiplexer_1_out), .in1(A_in), .out(PC_out), .sel(Register_in));
endmodule

module ByteExtract (
  input  Byte_Enable,
  input  [31:0] Input,
  input  Signed,
  input  [3:0] ByteSelect,
  output [31:0] Output
);

  wire and_5_out;
  wire [7:0] and_1_out, and_2_out, and_3_out, and_4_out, bit_extender_1_out, bit_extender_2_out,
       bit_extender_3_out, bit_extender_4_out, or_1_out;
  wire [31:0] bit_extender_5_out;

  assign bit_extender_1_out = {{7{ByteSelect[0]}}, ByteSelect[0]};  // Bit_Extender bit_extender_1
  assign bit_extender_2_out = {{7{ByteSelect[1]}}, ByteSelect[1]};  // Bit_Extender bit_extender_2
  assign bit_extender_3_out = {{7{ByteSelect[2]}}, ByteSelect[2]};  // Bit_Extender bit_extender_3
  assign bit_extender_4_out = {{7{ByteSelect[3]}}, ByteSelect[3]};  // Bit_Extender bit_extender_4
  assign and_1_out = Input[7:0] & bit_extender_1_out;  // AND_Gate and_1, 8 bits wide
  assign and_2_out = Input[15:8] & bit_extender_2_out;  // AND_Gate and_2, 8 bits wide
  assign and_3_out = Input[23:16] & bit_extender_3_out;  // AND_Gate and_3, 8 bits wide
  assign and_4_out = Input[31:24] & bit_extender_4_out;  // AND_Gate and_4, 8 bits wide
  assign or_1_out = and_1_out | and_2_out | and_3_out | and_4_out;  // OR_Gate or_1, 8 bits wide
  and and_5 (and_5_out, Signed, or_1_out[7]);
  Multiplexer #(.width(32), .enable("false")) multiplexer_1 (
    .in0(Input), .in1(bit_extender_5_out), .out(Output), .sel(Byte_Enable));
  assign bit_extender_5_out = {{24{and_5_out}}, or_1_out};  // Bit_Extender bit_extender_5
endmodule

module Linking (
  input  [4:0] rd_in,
  input  Link_Enable,
  input  [31:0] C_in,
  input  [31:0] Link_Address,
  output [4:0] rd_out,
  output [31:0] C_out
);

  wire [4:0] bit_extender_1_out;

  assign bit_extender_1_out = {{4{Link_Enable}}, Link_Enable};  // Bit_Extender bit_extender_1
  assign rd_out = rd_in | bit_extender_1_out;  // OR_Gate or_1, 5 bits wide
  Multiplexer #(.width(32), .enable("false")) multiplexer_1 (
    .in0(C_in), .in1(Link_Address), .out(C_out), .sel(Link_Enable));
endmodule

module rsrt_equals_rd (
  input  [4:0] rs,
  input  [4:0] rd,
  input  [4:0] rt,
  output Load_Forward
);

  wire nor_1_out, nor_2_out;
  wire [4:0] xor_1_out, xor_2_out;

  assign xor_1_out = rs ^ rd;  // XOR_Gate xor_1, 5 bits wide
  assign xor_2_out = rd ^ rt;  // XOR_Gate xor_2, 5 bits wide
  nor nor_1 (nor_1_out, xor_1_out[0], xor_1_out[1], xor_1_out[2], xor_1_out[3], xor_1_out[4]);
  nor nor_2 (nor_2_out, xor_2_out[0], xor_2_out[1], xor_2_out[2], xor_2_out[3], xor_2_out[4]);
  or or_1 (Load_Forward, nor_1_out, nor_2_out);
endmodule

module Disable_Load (
  input  WER_in,
  input  WED_in,
  input  LoadStall,
  input  Jump_in,
  input  Mux2_in,
  output WER_out,
  output WED_out,
  output Jump_out,
  output Mux2_out
);

  wire not_1_out, not_2_out;

  not not_1 (not_1_out, LoadStall);
  not not_2 (not_2_out, LoadStall);
  and and_1 (WER_out, WER_in, not_1_out);
  and and_2 (WED_out, not_1_out, WED_in);
  and and_3 (Jump_out, Jump_in, not_2_out);
  and and_4 (Mux2_out, not_2_out, Mux2_in);
endmodule
