// Logisim project decode.circ as structural Verilog
module I___J_Out (
  input  B0,
  input  B1,
  input  B2,
  input  B3,
  input  B4,
  input  B5,
  output O0,
  output O1,
  output O2,
  output O3,
  output MUX1,
  output MUX2,
  output SA,
  output Signed,
  output WE1,
  output WE2,
  output Extend,
  output SL,
  output L_S_Byte_or_Word,
  output Jump_Branch_Enable,
  output Link
);

  wire and_1_out, and_2_out, and_3_out, and_4_out, and_5_out, and_7_out, and_9_out, and_10_out, and_11_out,
       and_12_out, and_13_out, and_14_out, and_15_out, and_16_out, and_17_out, and_18_out, and_19_out,
       and_20_out, and_21_out, and_22_out, and_23_out, and_24_out, and_25_out, and_26_out, and_27_out,
       and_28_out, and_29_out, and_30_out, and_31_out, and_32_out, and_33_out, and_34_out, and_35_out,
       and_36_out, and_40_out, and_41_out, and_44_out, nand_1_out, nor_1_out, not_1_out, not_2_out,
       not_3_out, not_4_out, not_5_out, not_6_out, not_7_out, not_8_out, not_9_out, not_10_out, not_11_out,
       not_12_out, not_13_out, not_14_out, not_15_out, not_16_out, not_17_out, not_18_out, not_19_out,
       not_20_out, not_21_out, not_22_out, not_23_out, not_24_out, not_25_out, not_26_out, not_27_out,
       not_28_out, not_29_out, not_30_out, not_31_out, not_32_out, not_33_out, not_34_out, not_35_out,
       not_36_out, not_37_out, not_38_out, not_39_out, not_40_out, not_41_out, not_42_out, not_43_out,
       not_44_out, not_45_out, not_46_out, not_47_out, not_48_out, not_49_out, not_50_out, not_51_out,
       not_52_out, not_53_out, not_54_out, not_55_out, not_56_out, not_57_out, not_58_out, not_59_out,
       not_60_out, not_61_out, not_62_out, not_63_out, not_64_out, not_65_out, not_66_out, not_67_out,
       not_68_out, not_69_out, not_70_out, not_71_out, not_72_out, not_73_out, not_74_out, or_1_out,
       or_2_out, or_3_out, or_4_out, or_5_out, or_6_out, or_7_out, xnor_1_out, xnor_2_out, xnor_3_out,
       xnor_4_out, xnor_5_out, xnor_6_out;

  not not_1 (not_1_out, B5);
  not not_2 (not_2_out, B4);
  not not_3 (not_3_out, B2);
  not not_4 (not_4_out, B1);
  not not_5 (not_5_out, B2);
  not not_6 (not_6_out, B4);
  not not_7 (not_7_out, B2);
  not not_8 (not_8_out, B0);
  not not_9 (not_9_out, B2);
  not not_10 (not_10_out, B2);
  not not_11 (not_11_out, B1);
  not not_12 (not_12_out, B5);
  and and_1 (and_1_out, not_12_out, not_13_out, not_14_out);
  not not_13 (not_13_out, B4);
  not not_14 (not_14_out, B3);
  not not_15 (not_15_out, B4);
  not not_16 (not_16_out, B2);
  not not_17 (not_17_out, B5);
  not not_18 (not_18_out, B4);
  and and_2 (and_2_out, B5, not_19_out, not_20_out);
  not not_19 (not_19_out, B4);
  not not_20 (not_20_out, B3);
  not not_21 (not_21_out, B1);
  and and_3 (and_3_out, B2, not_21_out, not_22_out);
  not not_22 (not_22_out, B0);
  not not_23 (not_23_out, B2);
  not not_24 (not_24_out, B5);
  not not_25 (not_25_out, B4);
  not not_26 (not_26_out, B2);
  not not_27 (not_27_out, B0);
  not not_28 (not_28_out, B4);
  not not_29 (not_29_out, B2);
  not not_30 (not_30_out, B5);
  not not_31 (not_31_out, B4);
  not not_32 (not_32_out, B2);
  not not_33 (not_33_out, B1);
  not not_34 (not_34_out, B0);
  not not_35 (not_35_out, B4);
  and and_4 (and_4_out, B5, not_35_out, not_36_out);
  not not_36 (not_36_out, B3);
  and and_5 (and_5_out, B2, not_37_out, not_38_out);
  not not_37 (not_37_out, B1);
  not not_38 (not_38_out, B0);
  not not_39 (not_39_out, B2);
  not not_40 (not_40_out, B4);
  not not_41 (not_41_out, B2);
  not not_42 (not_42_out, B2);
  not not_43 (not_43_out, B1);
  not not_44 (not_44_out, B2);
  not not_45 (not_45_out, B5);
  not not_46 (not_46_out, B4);
  not not_47 (not_47_out, B3);
  not not_48 (not_48_out, B2);
  not not_49 (not_49_out, B5);
  not not_50 (not_50_out, B4);
  not not_51 (not_51_out, B4);
  not not_52 (not_52_out, B2);
  not not_53 (not_53_out, B1);
  not not_54 (not_54_out, B0);
  not not_55 (not_55_out, B5);
  not not_56 (not_56_out, B4);
  and and_6 (Jump_Branch_Enable, not_55_out, not_56_out, not_57_out);
  not not_57 (not_57_out, B3);
  not not_58 (not_58_out, B2);
  and and_7 (and_7_out, not_58_out, B1, B0);
  and and_8 (O0, not_1_out, not_2_out, B3, not_3_out, B1);
  and and_9 (and_9_out, not_4_out, B0);
  and and_10 (and_10_out, not_5_out, B1);
  and and_11 (and_11_out, B2, B1, B0);
  and and_12 (and_12_out, B5, not_6_out);
  and and_13 (and_13_out, and_12_out, and_14_out);
  and and_14 (and_14_out, not_7_out, xnor_1_out);
  xnor xnor_1 (xnor_1_out, B1, B0);
  not not_59 (not_59_out, B4);
  not not_60 (not_60_out, B3);
  and and_15 (and_15_out, B5, not_59_out, not_60_out, B2, not_61_out, not_62_out);
  not not_61 (not_61_out, B1);
  not not_62 (not_62_out, B0);
  and and_16 (and_16_out, B2, B1, not_8_out);
  and and_17 (and_17_out, not_9_out, B1);
  and and_18 (and_18_out, not_10_out, not_11_out, B0);
  and and_19 (and_19_out, B2, B1, B0);
  and and_20 (and_20_out, B5, not_15_out);
  and and_21 (and_21_out, and_20_out, and_22_out);
  and and_22 (and_22_out, not_16_out, xnor_2_out);
  xnor xnor_2 (xnor_2_out, B1, B0);
  not not_63 (not_63_out, B4);
  not not_64 (not_64_out, B3);
  and and_23 (and_23_out, B5, not_63_out, not_64_out, B2, not_65_out, not_66_out);
  not not_65 (not_65_out, B1);
  not not_66 (not_66_out, B0);
  and and_24 (and_24_out, not_17_out, not_18_out, B3);
  or or_1 (or_1_out, and_3_out, and_25_out);
  and and_25 (and_25_out, not_23_out, xnor_3_out);
  xnor xnor_3 (xnor_3_out, B1, B0);
  and and_26 (and_26_out, not_24_out, not_25_out, B3, not_26_out, B1, not_27_out);
  and and_27 (and_27_out, B5, not_28_out);
  and and_28 (and_28_out, and_27_out, and_29_out);
  and and_29 (and_29_out, not_29_out, xnor_4_out);
  xnor xnor_4 (xnor_4_out, B1, B0);
  and and_30 (and_30_out, not_30_out, not_31_out, B3);
  nand nand_1 (nand_1_out, not_32_out, not_33_out, not_34_out);
  or or_2 (or_2_out, and_5_out, and_31_out);
  and and_31 (and_31_out, not_39_out, xnor_5_out);
  xnor xnor_5 (xnor_5_out, B1, B0);
  xnor xnor_6 (xnor_6_out, B1, B0);
  not not_67 (not_67_out, B5);
  not not_68 (not_68_out, B4);
  and and_32 (and_32_out, not_67_out, not_68_out, B3);
  and and_33 (and_33_out, not_42_out, not_43_out, B0);
  or or_3 (or_3_out, and_33_out, and_34_out);
  and and_34 (and_34_out, not_44_out, B1);
  and and_35 (and_35_out, not_45_out, not_46_out, not_47_out, not_48_out, B1);
  and and_36 (and_36_out, not_49_out, not_50_out, B3, B2, B1, B0);
  and and_37 (L_S_Byte_or_Word, B5, not_51_out, not_52_out, not_53_out, not_54_out);
  and and_38 (Link, Jump_Branch_Enable, and_7_out);
  not not_69 (not_69_out, B5);
  not not_70 (not_70_out, B4);
  or or_4 (or_4_out, and_9_out, and_10_out, and_11_out);
  or or_5 (or_5_out, and_13_out, and_15_out);
  not not_71 (not_71_out, B5);
  not not_72 (not_72_out, B4);
  or or_6 (or_6_out, and_16_out, and_17_out);
  not not_73 (not_73_out, B5);
  not not_74 (not_74_out, B4);
  nor nor_1 (nor_1_out, and_18_out, and_19_out);
  or or_7 (or_7_out, and_21_out, and_23_out);
  and and_39 (MUX2, and_2_out, or_1_out);
  and and_40 (and_40_out, and_30_out, nand_1_out);
  and and_41 (and_41_out, and_4_out, or_2_out);
  and and_42 (WE2, B5, not_40_out, B3, not_41_out, xnor_6_out);
  and and_43 (Extend, and_32_out, or_3_out);
  and and_44 (and_44_out, not_69_out, not_70_out, B3, or_4_out);
  or or_8 (O1, and_44_out, or_5_out);
  and and_45 (O2, not_71_out, not_72_out, B3, or_6_out);
  and and_46 (O3, not_73_out, not_74_out, B3, nor_1_out);
  or or_9 (MUX1, and_1_out, or_7_out, and_24_out);
  or or_10 (Signed, and_26_out, and_28_out);
  or or_11 (WE1, and_40_out, and_41_out);
  or or_12 (SL, and_35_out, and_36_out);

  assign SA = 1'b1;
endmodule

module R_Out (
  input  B0,
  input  B1,
  input  B2,
  input  B3,
  input  B4,
  input  B5,
  output O0,
  output O1,
  output O2,
  output O3,
  output MUX1,
  output MUX2,
  output SA,
  output Signed,
  output WE1,
  output WE2,
  output Jump_Branch_Enable,
  output Link
);

  wire and_1_out, and_2_out, and_3_out, and_4_out, and_5_out, and_6_out, and_7_out, and_8_out, and_9_out,
       and_10_out, and_11_out, and_12_out, and_14_out, and_15_out, and_16_out, and_17_out, and_18_out,
       and_22_out, and_23_out, and_24_out, and_25_out, and_26_out, nand_1_out, nand_2_out, not_1_out,
       not_2_out, not_3_out, not_4_out, not_5_out, not_6_out, not_7_out, not_8_out, not_9_out, not_10_out,
       not_11_out, not_12_out, not_13_out, not_14_out, not_15_out, not_16_out, not_17_out, not_18_out,
       not_19_out, not_20_out, not_21_out, not_22_out, not_23_out, not_24_out, not_25_out, not_26_out,
       not_27_out, not_28_out, not_29_out, not_30_out, not_31_out, not_32_out, not_33_out, not_34_out,
       not_35_out, not_36_out, not_37_out, not_38_out, not_39_out, not_40_out, not_41_out, not_42_out,
       not_43_out, not_44_out, not_45_out, not_46_out, not_47_out, not_48_out, not_49_out, not_50_out,
       not_51_out, or_1_out, or_3_out, or_4_out;

  not not_1 (not_1_out, B4);
  not not_2 (not_2_out, B2);
  not not_3 (not_3_out, B5);
  not not_4 (not_4_out, B4);
  not not_5 (not_5_out, B2);
  not not_6 (not_6_out, B5);
  not not_7 (not_7_out, B4);
  not not_8 (not_8_out, B3);
  not not_9 (not_9_out, B2);
  not not_10 (not_10_out, B1);
  not not_11 (not_11_out, B2);
  not not_12 (not_12_out, B1);
  not not_13 (not_13_out, B2);
  not not_14 (not_14_out, B4);
  not not_15 (not_15_out, B3);
  not not_16 (not_16_out, B4);
  not not_17 (not_17_out, B2);
  not not_18 (not_18_out, B1);
  not not_19 (not_19_out, B4);
  not not_20 (not_20_out, B2);
  not not_21 (not_21_out, B0);
  not not_22 (not_22_out, B4);
  not not_23 (not_23_out, B2);
  not not_24 (not_24_out, B4);
  not not_25 (not_25_out, B3);
  not not_26 (not_26_out, B5);
  not not_27 (not_27_out, B4);
  not not_28 (not_28_out, B3);
  not not_29 (not_29_out, B1);
  not not_30 (not_30_out, B5);
  not not_31 (not_31_out, B4);
  not not_32 (not_32_out, B2);
  not not_33 (not_33_out, B1);
  and and_1 (and_1_out, B5, not_1_out, B3, not_2_out, B1);
  and and_2 (and_2_out, not_3_out, not_4_out, B3, not_5_out, B1);
  and and_3 (and_3_out, not_6_out, not_7_out, not_8_out, B1, B0);
  and and_4 (and_4_out, not_9_out, not_10_out, B0);
  and and_5 (and_5_out, not_11_out, B1, B0);
  and and_6 (and_6_out, B2, not_12_out, B0);
  and and_7 (and_7_out, B2, B1, B0);
  not not_34 (not_34_out, B5);
  and and_8 (and_8_out, not_34_out, not_35_out);
  not not_35 (not_35_out, B0);
  and and_9 (and_9_out, not_13_out, B1, B0);
  and and_10 (and_10_out, B2, B1);
  and and_11 (and_11_out, B5, not_14_out, not_15_out, B2);
  and and_12 (and_12_out, not_16_out, B3, not_17_out, B1);
  not not_36 (not_36_out, B5);
  not not_37 (not_37_out, B4);
  not not_38 (not_38_out, B3);
  nand nand_1 (nand_1_out, not_18_out, B0);
  and and_13 (Signed, B5, not_19_out, B3, not_20_out, B1, not_21_out);
  and and_14 (and_14_out, not_22_out, B3, not_23_out, B1);
  and and_15 (and_15_out, B5, not_24_out, not_25_out);
  and and_16 (and_16_out, and_15_out, or_1_out);
  or or_1 (or_1_out, B2, B0);
  and and_17 (and_17_out, not_26_out, not_27_out, not_28_out);
  and and_18 (and_18_out, and_17_out, nand_2_out);
  nand nand_2 (nand_2_out, not_29_out, B0);
  and and_19 (Jump_Branch_Enable, not_30_out, not_31_out, B3, not_32_out, not_33_out);
  not not_39 (not_39_out, B0);
  or or_2 (O0, and_1_out, and_2_out, and_3_out);
  not not_40 (not_40_out, B4);
  not not_41 (not_41_out, B3);
  or or_3 (or_3_out, and_4_out, and_5_out, and_6_out, and_7_out);
  not not_42 (not_42_out, and_8_out);
  not not_43 (not_43_out, B4);
  not not_44 (not_44_out, B2);
  not not_45 (not_45_out, B4);
  not not_46 (not_46_out, B3);
  or or_4 (or_4_out, and_9_out, and_10_out);
  not not_47 (not_47_out, B4);
  not not_48 (not_48_out, B2);
  not not_49 (not_49_out, B5);
  not not_50 (not_50_out, B4);
  not not_51 (not_51_out, B3);
  or or_5 (O3, and_11_out, and_12_out);
  and and_20 (SA, not_36_out, not_37_out, not_38_out, B2, nand_1_out);
  and and_21 (Link, Jump_Branch_Enable, not_39_out);
  and and_22 (and_22_out, B5, not_40_out, not_41_out, or_3_out);
  and and_23 (and_23_out, not_42_out, not_43_out, B3, not_44_out, B1);
  and and_24 (and_24_out, B5, not_45_out, not_46_out, or_4_out);
  and and_25 (and_25_out, B5, not_47_out, B3, not_48_out, B1);
  and and_26 (and_26_out, not_49_out, not_50_out, not_51_out, B1);
  or or_6 (O1, and_22_out, and_23_out);
  or or_7 (O2, and_24_out, and_25_out, and_26_out);
  or or_8 (WE1, and_14_out, and_16_out, and_18_out);

  assign MUX1 = 1'b0;
  assign MUX2 = 1'b0;
  assign WE2 = 1'b0;
endmodule

module De (
  input  [5:0] Op,
  input  [5:0] Func,
  output SAsel,
  output [3:0] ALU_code,
  output MUX1,
  output MUX2,
  output WriteEnable1,
  output WriteEnable2,
  output Signed,
  output [1:0] Extend,
  output Load_Store_Byte_vs_Word,
  output Jump_Branch_Enable,
  output Link
);

  wire i_j_out_1_jump_branch_enable, i_j_out_1_link, i_j_out_1_mux1, i_j_out_1_mux2, i_j_out_1_sa,
       i_j_out_1_signed, i_j_out_1_we1, i_j_out_1_we2, nor_1_out, r_out_1_jump_branch_enable, r_out_1_link,
       r_out_1_mux1, r_out_1_mux2, r_out_1_sa, r_out_1_signed, r_out_1_we1, r_out_1_we2;
  wire [3:0] i_j_out_1_o0;

  nor nor_1 (nor_1_out, Op[0], Op[1], Op[2], Op[3], Op[4], Op[5]);
  I___J_Out i_j_out_1 (
    .B0(Op[0]), .B1(Op[1]), .B2(Op[2]), .B3(Op[3]), .B4(Op[4]), .B5(Op[5]), .O0(i_j_out_1_o0[0]),
    .O1(i_j_out_1_o0[1]), .O2(i_j_out_1_o0[2]), .O3(i_j_out_1_o0[3]), .MUX1(i_j_out_1_mux1),
    .MUX2(i_j_out_1_mux2), .SA(i_j_out_1_sa), .Signed(i_j_out_1_signed), .WE1(i_j_out_1_we1),
    .WE2(i_j_out_1_we2), .Extend(Extend[1]), .SL(Extend[0]), .L_S_Byte_or_Word(Load_Store_Byte_vs_Word),
    .Jump_Branch_Enable(i_j_out_1_jump_branch_enable), .Link(i_j_out_1_link));
  R_Out r_out_1 (
    .B0(Func[0]), .B1(Func[1]), .B2(Func[2]), .B3(Func[3]), .B4(Func[4]), .B5(Func[5]),
    .O0(Load_Store_Byte_vs_Word), .O1(Load_Store_Byte_vs_Word), .O2(Load_Store_Byte_vs_Word),
    .O3(Load_Store_Byte_vs_Word), .MUX1(r_out_1_mux1), .MUX2(r_out_1_mux2), .SA(r_out_1_sa),
    .Signed(r_out_1_signed), .WE1(r_out_1_we1), .WE2(r_out_1_we2),
    .Jump_Branch_Enable(r_out_1_jump_branch_enable), .Link(r_out_1_link));
  Multiplexer #(.width(4), .enable("false")) multiplexer_1 (
    .in0(i_j_out_1_o0), .in1({4{Load_Store_Byte_vs_Word}}), .out(ALU_code), .sel(nor_1_out));
  Multiplexer #(.enable("false")) multiplexer_2 (.in0(i_j_out_1_mux1), .in1(r_out_1_mux1), .out(MUX1), .sel(nor_1_out));
  Multiplexer #(.enable("false")) multiplexer_3 (.in0(i_j_out_1_mux2), .in1(r_out_1_mux2), .out(MUX2), .sel(nor_1_out));
  Multiplexer #(.enable("false")) multiplexer_4 (.in0(i_j_out_1_sa), .in1(r_out_1_sa), .out(SAsel), .sel(nor_1_out));
  Multiplexer #(.enable("false")) multiplexer_5 (
    .in0(i_j_out_1_signed), .in1(r_out_1_signed), .out(Signed), .sel(nor_1_out));
  Multiplexer #(.enable("false")) multiplexer_6 (
    .in0(i_j_out_1_we1), .in1(r_out_1_we1), .out(WriteEnable1), .sel(nor_1_out));
  Multiplexer #(.enable("false")) multiplexer_7 (
    .in0(i_j_out_1_we2), .in1(r_out_1_we2), .out(WriteEnable2), .sel(nor_1_out));
  Multiplexer #(.enable("false")) multiplexer_8 (
    .in0(i_j_out_1_jump_branch_enable), .in1(r_out_1_jump_branch_enable), .out(Jump_Branch_Enable),
    .sel(nor_1_out));
  Multiplexer #(.enable("false")) multiplexer_9 (.in0(i_j_out_1_link), .in1(r_out_1_link), .out(Link), .sel(nor_1_out));
endmodule
